# Fritzing sketch Sketch (saved by Fritzing 0.9.4)
circuit board: 6.59219cm x 5.19965cm
breadboards: 1

parts:
  100k = Resistor [tolerance=±5% resistance=100k package=THT]
  U1 = ESP32S-HiLetgo [part_number=ESP32S-HiLetgo]
  RJ12 = RJ12
  U2 = LM2596 step down module [part_number="In:12V, Out: 5V"]
  1N4001 = Diode [package=diode-1n4148]

nets:
  N1: 100k.Pin_0, U1.GPIO22, RJ12.pin_4, 1N4001.A
  N2: 100k.Pin_1, U1.3.3
  N3: U1.GND, RJ12.pin_5, U2.IN-, U2.OUT-
  N4: U1.VIN, U2.OUT+
  N5: U1.GPIO21, RJ12.pin_6
  N6: U1.GPIO23, 1N4001.C
  N7: RJ12.pin_3, U2.IN+

custom parts:
  ESP32S-HiLetgo: HiLetgo ESP-WROOM-32 ESP32 ESP-32S Development Board 2.4GHz Dual-Mode WiFi + Bluetooth Dual Cores Microcontroller The ESP32 integrated with Antenna switches, RF Balun, power amplifiers, low-noise amplifiers, filters, and management modules, and the entire solution occupies the least area of PCB. 2.4 GHz Wi-Fi plus Bluetooth dual-mode chip, with TSMC Ultra-low power consumption 40nm technology,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
  LM2596 step down module: LM2596 DC-DC step down power supply module 3 A.
